# Fritzing sketch Com_Serial_RPI-Pico_Sketch (saved by Fritzing 0.9.3b)
breadboards: 1

parts:
  Pico_H1 = Raspberry Pi Pico H
  R1 = Resistor [tolerance=±5% resistance=220 package=THT]
  LED1 = LED - 5mm [color="Red (633nm)" package="5 mm [THT]"]
  LED2 = LED - 5mm [color="Red (633nm)" package="5 mm [THT]"]
  LED3 = LED - 5mm [color="Red (633nm)" package="5 mm [THT]"]
  LED4 = LED - 5mm [color="Red (633nm)" package="5 mm [THT]"]
  LED5 = LED - 5mm [color="Red (633nm)" package="5 mm [THT]"]
  S1 = Pushbutton [package="[THT]"]

nets:
  N1: Pico_H1.GND, R1.Pin_1
  N2: Pico_H1.3V3, S1.Pin_3, S1.Pin_4
  N3: Pico_H1.GP16, S1.Pin_1, S1.Pin_2
  N4: Pico_H1.GP4, LED1.anode
  N5: Pico_H1.GP3, LED2.anode
  N6: Pico_H1.GP2, LED3.anode
  N7: Pico_H1.GP1, LED4.anode
  N8: Pico_H1.GP0, LED5.anode
  N9: R1.Pin_0, LED1.cathode, LED2.cathode, LED3.cathode, LED4.cathode, LED5.cathode

custom parts:
  Raspberry Pi Pico H: Raspberry Pi Pico H. Based around the RP2040 microcontroller the Pico H is a low cost microcontroller device bringing Raspberry Pi quality, cost, and easy of use to the microcontroller space.
