# Fritzing sketch Hilos_RPI-Pico (saved by Fritzing 0.9.3b)
breadboards: 1

parts:
  R1 = Resistor [tolerance=±5% resistance=220 package=THT]
  Pico_H1 = Raspberry Pi Pico H
  LED1 = smd LED [color="Red (633nm)" package="1206 [SMD]"]
  LED2 = smd LED [color="Red (633nm)" package="1206 [SMD]"]
  LED3 = smd LED [color="Red (633nm)" package="1206 [SMD]"]
  LED4 = smd LED [color="Red (633nm)" package="1206 [SMD]"]
  LED5 = smd LED [color="Red (633nm)" package="1206 [SMD]"]
  S1 = Pushbutton [package="[THT]"]
  S2 = Pushbutton [package="[THT]"]
  S3 = Pushbutton [package="[THT]"]
  S4 = Pushbutton [package="[THT]"]
  S5 = Pushbutton [package="[THT]"]
  S6 = Pushbutton [package="[THT]"]

nets:
  N1: R1.Pin_0, LED1.cathode, LED2.cathode, LED3.cathode, LED4.cathode, LED5.cathode
  N2: R1.Pin_1, Pico_H1.GND
  N3: Pico_H1.3V3, S2.Pin_3, S2.Pin_4, S3.Pin_3, S3.Pin_4, S4.Pin_3, S4.Pin_4, S5.Pin_3, S5.Pin_4, S6.Pin_3, S6.Pin_4
  N4: Pico_H1.GP18, S1.Pin_1, S1.Pin_2
  N5: Pico_H1.GP17, S6.Pin_1, S6.Pin_2
  N6: Pico_H1.GP16, S5.Pin_1, S5.Pin_2
  N7: Pico_H1.GP15, S4.Pin_1, S4.Pin_2
  N8: Pico_H1.GP14, S2.Pin_1, S2.Pin_2
  N9: Pico_H1.GP13, S3.Pin_1, S3.Pin_2
  N10: Pico_H1.GP4, LED5.anode
  N11: Pico_H1.GP3, LED4.anode
  N12: Pico_H1.GP2, LED3.anode
  N13: Pico_H1.GP1, LED2.anode
  N14: Pico_H1.GP0, LED1.anode
  N15: S1.Pin_3, S1.Pin_4

custom parts:
  Raspberry Pi Pico H: Raspberry Pi Pico H. Based around the RP2040 microcontroller the Pico H is a low cost microcontroller device bringing Raspberry Pi quality, cost, and easy of use to the microcontroller space.
